# Fritzing sketch pcb (saved by Fritzing 0.9.9b)
circuit board: 11.8162cm x 7.66236cm
breadboards: 1

parts:
  U1 = atmega328 [package=dip]
  S1 = Pushbutton [package="[THT]"]
  S2 = Pushbutton [package="[THT]"]
  S3 = Pushbutton [package="[THT]"]
  S4 = Pushbutton [package="[THT]"]
  Nokia_5110_LCD_Module1 = Nokia 5110 LCD
  S5 = Pushbutton [package="[THT]"]
  LED1 = LEDs [package=led10mm]
  LED2 = LEDs [package=led10mm]
  R1 = Resistor [tolerance=±5% power=0.25 resistance=220 package=THT]
  R2 = Resistor [tolerance=±5% power=0.25 resistance=220 package=THT]
  VCC1 = Battery
  J1 = female pin header, 6 pins [form="♀ (female)"]
  XTAL1 = Crystal [frequency="16 Mhz" package=THT]
  C1 = Capacitor [package=cap-pth-small2]
  C2 = Capacitor [package=cap-pth-small2]

nets:
  N1: U1.RESET, J1.pin6
  N2: U1.D0_(RX), J1.pin4
  N3: U1.D1_(TX), J1.pin5
  N4: U1.D2, R2.Pin_1
  N5: U1.D3_(PWM), Nokia_5110_LCD_Module1.RST, Nokia_5110_LCD_Module1.RST_(out)
  N6: U1.D4, Nokia_5110_LCD_Module1.SCE, Nokia_5110_LCD_Module1.SCE_(out)
  VCC: U1.VCC, U1.AVCC, Nokia_5110_LCD_Module1.VCC, Nokia_5110_LCD_Module1.LED, Nokia_5110_LCD_Module1.VCC_(out), Nokia_5110_LCD_Module1.LED_(out), VCC1.+, J1.pin3
  GND: U1.GND, S1.Pin_1, S1.Pin_2, S2.Pin_1, S2.Pin_2, S3.Pin_1, S3.Pin_2, S4.Pin_1, S4.Pin_2, Nokia_5110_LCD_Module1.GND, Nokia_5110_LCD_Module1.GND_(out), S5.Pin_1, S5.Pin_2, LED1.C, LED2.C, VCC1.-, J1.pin1, C1.2, C2.2
  N7: U1.XLAT1, XTAL1.pin_0, C2.1
  N8: U1.XLAT2, XTAL1.pin_1, C1.1
  N9: U1.D5_(PWM), Nokia_5110_LCD_Module1.D/C, Nokia_5110_LCD_Module1.D/C_(out)
  N10: U1.D6_(PWM), Nokia_5110_LCD_Module1.DN(MOSI), Nokia_5110_LCD_Module1.DN(MODI)_(out)
  N11: U1.D7, Nokia_5110_LCD_Module1.SCLK, Nokia_5110_LCD_Module1.SCLK_(out)
  N12: U1.D8, R1.Pin_0
  N13: U1.D9_(PWM), S4.Pin_3, S4.Pin_4
  N14: U1.D10_(PWM), S1.Pin_3, S1.Pin_4
  N15: U1.D11_(PWM), S2.Pin_3, S2.Pin_4
  N16: U1.D12, S3.Pin_3, S3.Pin_4
  N17: U1.D13, S5.Pin_3, S5.Pin_4
  N18: LED1.A, R1.Pin_1
  N19: LED2.A, R2.Pin_0

notes:
  Build'IT

custom parts:
  Nokia 5110 LCD: Nokia 5110 Graphic 84*48 LCD module such as the Sparkfun LCD-10168 or the clones from Ebay. There is example code for the Arduino available from the Sparkfun site in https://learn.sparkfun.com/tutorials/graphic-lcd-hookup-guide This is a 3.3V device, if you are running it from a 5V micro you need a 5V tolorant level translator such as the 74ahc367 to protect the signal imputs. Rafa G. did a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
